// Logisim project LAB-03_Design a 3-bit by 3-bit Binary Multiplication Unit.circ as structural Verilog: 1 circuit, main circuit main
module main (
  input  [2:0] B,
  input  [2:0] A,
  output [5:0] S5_S4_S3_S2_S1_S0
);

  wire [1:0] A1B2_out;
  wire [2:0] A2B1_out, A3B1_out, adder_1_cout;

  and A3B3 (A3B1_out[2], A[2], B[2]);
  and A3B1 (A3B1_out[0], A[2], B[0]);
  and A3B2 (A3B1_out[1], A[2], B[1]);
  and A2B3 (A2B1_out[2], A[1], B[2]);
  and A2B2 (A2B1_out[1], A[1], B[1]);
  and A2B1 (A2B1_out[0], A[1], B[0]);
  and A1B2 (A1B2_out[0], A[0], B[1]);
  and A1B3 (A1B2_out[1], A[0], B[2]);
  and A1B1 (S5_S4_S3_S2_S1_S0[0], A[0], B[0]);
  Adder #(.width(3)) adder_1 (
    .a({1'b0, A1B2_out}), .b(A2B1_out), .out({adder_1_cout[1:0], S5_S4_S3_S2_S1_S0[1]}), .cin(1'b0),
    .cout(adder_1_cout[2]));
  Adder #(.width(3)) adder_2 (
    .a(A3B1_out), .b(adder_1_cout), .out(S5_S4_S3_S2_S1_S0[4:2]), .cin(1'b0), .cout(S5_S4_S3_S2_S1_S0[5]));

  // Notes on the sheet:
  //   Fig: A 3-bit by 3-bit Binary Multiplier
  //   Sudipto Roy
  //   ID: 2222756042
endmodule
