// Logisim project LAB-04_Design of a 3-bit Binary Up-Down counter.circ as structural Verilog: 1 circuit, main circuit main
module main (
  input  M,
  input  CLR,
  output Qc,
  output Qb,
  output Qa
);

  wire and_1_out, and_2_out, and_3_out, and_4_out, CLK_out, not_1_out, or_1_out, or_2_out, t_ff_1_qn,
       t_ff_2_qn;

  Clock CLK (.out(CLK_out));
  T_Flip_Flop t_ff_1 (.T(1'b1), .clk(CLK_out), .Q(Qa), .Qn(t_ff_1_qn), .reset(CLR));  // open: preset
  not not_1 (not_1_out, M);
  and and_1 (and_1_out, not_1_out, Qa);
  and and_2 (and_2_out, t_ff_1_qn, M);
  or or_1 (or_1_out, and_1_out, and_2_out);
  T_Flip_Flop t_ff_2 (.T(or_1_out), .clk(CLK_out), .Q(Qb), .Qn(t_ff_2_qn), .reset(CLR));  // open: preset
  and and_3 (and_3_out, and_1_out, Qb);
  and and_4 (and_4_out, t_ff_2_qn, and_2_out);
  or or_2 (or_2_out, and_3_out, and_4_out);
  T_Flip_Flop t_ff_3 (.T(or_2_out), .clk(CLK_out), .Q(Qc), .reset(CLR));  // open: Qn, preset

  // Notes on the sheet:
  //   Fig. Design of a 3-bit Binary Up-Down counter
  //   Sudipto Roy
  //   ID: 2222756042
endmodule
