// Logisim project LAB-06_Design of an ALU.circ as structural Verilog
module _1_bit_ALU (
  input  Cin,
  input  A,
  input  B,
  input  [1:0] SELECT,
  output RESULT,
  output Cout
);

  wire adder_1_out, and_1_out, and_2_out, multiplexer_1_out, not_1_out, or_1_out;

  not not_1 (not_1_out, B);
  Multiplexer multiplexer_1 (.in0(B), .in1(not_1_out), .out(multiplexer_1_out), .sel(and_1_out));  // open: en
  and and_1 (and_1_out, SELECT[0], SELECT[1]);
  and and_2 (and_2_out, A, B);
  or or_1 (or_1_out, A, B);
  Adder #(.width(1)) adder_1 (.a(A), .b(multiplexer_1_out), .out(adder_1_out), .cin(Cin), .cout(Cout));
  Multiplexer #(.select(2)) multiplexer_2 (
    .in0(and_2_out), .in1(or_1_out), .in2(adder_1_out), .in3(adder_1_out), .out(RESULT), .sel(SELECT));  // open: en

  // Notes on the sheet:
  //   Sudipto Roy
  //   ID: 2222756042
endmodule

module _16_bit_ALU (
  input  [1:0] SELECT,
  input  Cin,
  input  [15:0] A,
  input  [15:0] B,
  output [15:0] RESULT,
  output ZERO_SIGNAL,
  output Cout
);

  wire _0_cout, _1_cout, _2_cout, _3_cout, _4_cout, _5_cout, _6_cout, _7_cout, _8_cout, _9_cout, _10_cout,
       _11_cout, _12_cout, _13_cout, _14_cout;

  _1_bit_ALU _0 (.Cin(Cin), .A(A[0]), .B(B[0]), .RESULT(RESULT[0]), .Cout(_0_cout), .SELECT(SELECT));
  _1_bit_ALU _1 (.Cin(_0_cout), .A(A[1]), .B(B[1]), .RESULT(RESULT[1]), .Cout(_1_cout), .SELECT(SELECT));
  _1_bit_ALU _2 (.Cin(_1_cout), .A(A[2]), .B(B[2]), .RESULT(RESULT[2]), .Cout(_2_cout), .SELECT(SELECT));
  _1_bit_ALU _3 (.Cin(_2_cout), .A(A[3]), .B(B[3]), .RESULT(RESULT[3]), .Cout(_3_cout), .SELECT(SELECT));
  _1_bit_ALU _4 (.Cin(_3_cout), .A(A[4]), .B(B[4]), .RESULT(RESULT[4]), .Cout(_4_cout), .SELECT(SELECT));
  _1_bit_ALU _5 (.Cin(_4_cout), .A(A[5]), .B(B[5]), .RESULT(RESULT[5]), .Cout(_5_cout), .SELECT(SELECT));
  _1_bit_ALU _6 (.Cin(_5_cout), .A(A[6]), .B(B[6]), .RESULT(RESULT[6]), .Cout(_6_cout), .SELECT(SELECT));
  _1_bit_ALU _7 (.Cin(_6_cout), .A(A[7]), .B(B[7]), .RESULT(RESULT[7]), .Cout(_7_cout), .SELECT(SELECT));
  _1_bit_ALU _8 (.Cin(_7_cout), .A(A[8]), .B(B[8]), .RESULT(RESULT[8]), .Cout(_8_cout), .SELECT(SELECT));
  _1_bit_ALU _9 (.Cin(_8_cout), .A(A[9]), .B(B[9]), .RESULT(RESULT[9]), .Cout(_9_cout), .SELECT(SELECT));
  _1_bit_ALU _10 (.Cin(_9_cout), .A(A[10]), .B(B[10]), .RESULT(RESULT[10]), .Cout(_10_cout), .SELECT(SELECT));
  _1_bit_ALU _11 (.Cin(_10_cout), .A(A[11]), .B(B[11]), .RESULT(RESULT[11]), .Cout(_11_cout), .SELECT(SELECT));
  _1_bit_ALU _12 (.Cin(_11_cout), .A(A[12]), .B(B[12]), .RESULT(RESULT[12]), .Cout(_12_cout), .SELECT(SELECT));
  _1_bit_ALU _13 (.Cin(_12_cout), .A(A[13]), .B(B[13]), .RESULT(RESULT[13]), .Cout(_13_cout), .SELECT(SELECT));
  _1_bit_ALU _14 (.Cin(_13_cout), .A(A[14]), .B(B[14]), .RESULT(RESULT[14]), .Cout(_14_cout), .SELECT(SELECT));
  _1_bit_ALU _15 (.Cin(_14_cout), .A(A[15]), .B(B[15]), .RESULT(RESULT[15]), .Cout(Cout), .SELECT(SELECT));
  nor nor_1 (ZERO_SIGNAL, RESULT[0], RESULT[1], RESULT[2], RESULT[3], RESULT[4], RESULT[5], RESULT[6], RESULT[7], RESULT[8], RESULT[9], RESULT[10], RESULT[11], RESULT[12], RESULT[13], RESULT[14], RESULT[15]);

  // Notes on the sheet:
  //   Sudipto Roy
  //   ID: 2222756042
endmodule
