// Logisim project LAB-07_Build a single cycle datapath (R-type).circ as structural Verilog
module Instruction_Fetch_Unit (
  input  Clock,
  input  Clear,
  output [15:0] Data
);

  wire [1:0] adder_1_out, register_1_q;

  Register #(.width(2)) register_1 (.D(adder_1_out), .Q(register_1_q), .clk(Clock), .clr(Clear));  // open: en
  Adder #(.width(2)) adder_1 (.a(register_1_q), .b(2'b01), .out(adder_1_out));  // open: cin, cout
  ROM #(.addrWidth(2), .dataWidth(16)) rom_1 (.addr(register_1_q), .data(Data));  // open: sel

  // Notes on the sheet:
  //   16 bit ISA
  //   4 Instruction
  //   contents of rom_1 (hex, n*v repeats v):
  //   2070 213a 313f
endmodule

module R_Type_DataPath (
  input  Cin,
  input  [15:0] Result,
  input  CLOCK,
  input  CLEAR,
  input  REGISTER_WRITE,
  output Cout
);

  wire [1:0] bit_extender_1_out;
  wire [15:0] instruction_fetch_unit_1_data, registerfile_1_read_data_1, registerfile_1_read_data_2;

  Instruction_Fetch_Unit instruction_fetch_unit_1 (.Clock(CLOCK), .Clear(CLEAR), .Data(instruction_fetch_unit_1_data));
  RegisterFile registerfile_1 (
    .Write_Data(Result), .RD(instruction_fetch_unit_1_data[3:0]), .Read_Data_1(registerfile_1_read_data_1),
    .Read_Data_2(registerfile_1_read_data_2), .Reg_Write(REGISTER_WRITE), .CLK(CLOCK),
    .Read_Register_1__RS(instruction_fetch_unit_1_data[11:8]),
    .Read_Register_2__RT(instruction_fetch_unit_1_data[7:4]));
  Bit_Extender #(.in_width(4), .out_width(2)) bit_extender_1 (
    .in(instruction_fetch_unit_1_data[15:12]), .out(bit_extender_1_out));
  _16_bit_ALU u_16_bit_alu_1 (
    .RESULT(Result), .Cout(Cout), .A(registerfile_1_read_data_1), .B(registerfile_1_read_data_2),
    .SELECT(bit_extender_1_out), .Cin(Cin));  // open: ZERO_SIGNAL

  // Notes on the sheet:
  //   Sudipto Roy
  //   ID: 2222756042
endmodule

module RegisterFile (
  input  [15:0] Write_Data,
  input  [3:0] Read_Register_1__RS,
  input  [3:0] RD,
  input  [3:0] Read_Register_2__RT,
  input  Reg_Write,
  input  CLK,
  output [15:0] Read_Data_1,
  output [15:0] Read_Data_2
);

  wire and_1_out, and_2_out, and_3_out, and_4_out, and_5_out, and_6_out, and_7_out, and_8_out, and_9_out,
       and_10_out, and_11_out, and_12_out, and_13_out, and_14_out, and_15_out, and_16_out, decoder_1_out0,
       decoder_1_out1, decoder_1_out2, decoder_1_out3, decoder_1_out4, decoder_1_out5, decoder_1_out6,
       decoder_1_out7, decoder_1_out8, decoder_1_out9, decoder_1_out10, decoder_1_out11, decoder_1_out12,
       decoder_1_out13, decoder_1_out14, decoder_1_out15;
  wire [15:0] register_1_q, register_2_q, register_3_q, register_4_q, register_5_q, register_6_q,
       register_7_q, register_8_q, register_9_q, register_10_q, register_11_q, register_12_q, register_13_q,
       register_14_q, register_15_q, register_16_q;

  Decoder #(.select(4)) decoder_1 (
    .out0(decoder_1_out0), .out1(decoder_1_out1), .out2(decoder_1_out2), .out3(decoder_1_out3),
    .out4(decoder_1_out4), .out5(decoder_1_out5), .out6(decoder_1_out6), .out7(decoder_1_out7),
    .out8(decoder_1_out8), .out9(decoder_1_out9), .out10(decoder_1_out10), .out11(decoder_1_out11),
    .out12(decoder_1_out12), .out13(decoder_1_out13), .out14(decoder_1_out14), .out15(decoder_1_out15),
    .sel(RD));  // open: en
  and and_1 (and_1_out, Reg_Write, decoder_1_out0);
  and and_2 (and_2_out, Reg_Write, decoder_1_out1);
  and and_3 (and_3_out, Reg_Write, decoder_1_out2);
  and and_4 (and_4_out, Reg_Write, decoder_1_out3);
  and and_5 (and_5_out, Reg_Write, decoder_1_out4);
  and and_6 (and_6_out, Reg_Write, decoder_1_out5);
  and and_7 (and_7_out, Reg_Write, decoder_1_out6);
  and and_8 (and_8_out, Reg_Write, decoder_1_out7);
  and and_9 (and_9_out, Reg_Write, decoder_1_out8);
  and and_10 (and_10_out, Reg_Write, decoder_1_out9);
  and and_11 (and_11_out, Reg_Write, decoder_1_out10);
  and and_12 (and_12_out, Reg_Write, decoder_1_out11);
  and and_13 (and_13_out, Reg_Write, decoder_1_out12);
  and and_14 (and_14_out, Reg_Write, decoder_1_out13);
  and and_15 (and_15_out, Reg_Write, decoder_1_out14);
  and and_16 (and_16_out, Reg_Write, decoder_1_out15);
  Register #(.width(16)) register_1 (.D(Write_Data), .en(and_1_out), .Q(register_1_q), .clk(CLK));  // open: clr
  Register #(.width(16)) register_2 (.D(Write_Data), .en(and_2_out), .Q(register_2_q), .clk(CLK));  // open: clr
  Register #(.width(16)) register_3 (.D(Write_Data), .en(and_3_out), .Q(register_3_q), .clk(CLK));  // open: clr
  Register #(.width(16)) register_4 (.D(Write_Data), .en(and_4_out), .Q(register_4_q), .clk(CLK));  // open: clr
  Register #(.width(16)) register_5 (.D(Write_Data), .en(and_5_out), .Q(register_5_q), .clk(CLK));  // open: clr
  Register #(.width(16)) register_6 (.D(Write_Data), .en(and_6_out), .Q(register_6_q), .clk(CLK));  // open: clr
  Register #(.width(16)) register_7 (.D(Write_Data), .en(and_7_out), .Q(register_7_q), .clk(CLK));  // open: clr
  Register #(.width(16)) register_8 (.D(Write_Data), .en(and_8_out), .Q(register_8_q), .clk(CLK));  // open: clr
  Register #(.width(16)) register_9 (.D(Write_Data), .en(and_9_out), .Q(register_9_q), .clk(CLK));  // open: clr
  Register #(.width(16)) register_10 (.D(Write_Data), .en(and_10_out), .Q(register_10_q), .clk(CLK));  // open: clr
  Register #(.width(16)) register_11 (.D(Write_Data), .en(and_11_out), .Q(register_11_q), .clk(CLK));  // open: clr
  Register #(.width(16)) register_12 (.D(Write_Data), .en(and_12_out), .Q(register_12_q), .clk(CLK));  // open: clr
  Register #(.width(16)) register_13 (.D(Write_Data), .en(and_13_out), .Q(register_13_q), .clk(CLK));  // open: clr
  Register #(.width(16)) register_14 (.D(Write_Data), .en(and_14_out), .Q(register_14_q), .clk(CLK));  // open: clr
  Register #(.width(16)) register_15 (.D(Write_Data), .en(and_15_out), .Q(register_15_q), .clk(CLK));  // open: clr
  Register #(.width(16)) register_16 (.D(Write_Data), .en(and_16_out), .Q(register_16_q), .clk(CLK));  // open: clr
  Multiplexer #(.select(4), .width(16)) multiplexer_1 (
    .in0(register_1_q), .in1(register_2_q), .in2(register_3_q), .in3(register_4_q), .in4(register_5_q),
    .in5(register_6_q), .in6(register_7_q), .in7(register_8_q), .in8(register_9_q), .in9(register_10_q),
    .in10(register_11_q), .in11(register_12_q), .in12(register_13_q), .in13(register_14_q),
    .in14(register_15_q), .in15(register_16_q), .out(Read_Data_1), .sel(Read_Register_1__RS));  // open: en
  Multiplexer #(.select(4), .width(16)) multiplexer_2 (
    .in0(register_1_q), .in1(register_2_q), .in2(register_3_q), .in3(register_4_q), .in4(register_5_q),
    .in5(register_6_q), .in6(register_7_q), .in7(register_8_q), .in8(register_9_q), .in9(register_10_q),
    .in10(register_11_q), .in11(register_12_q), .in12(register_13_q), .in13(register_14_q),
    .in14(register_15_q), .in15(register_16_q), .out(Read_Data_2), .sel(Read_Register_2__RT));  // open: en
endmodule

module _16_bit_ALU (
  input  [1:0] SELECT,
  input  Cin,
  input  [15:0] A,
  input  [15:0] B,
  output [15:0] RESULT,
  output ZERO_SIGNAL,
  output Cout
);

  wire _0_cout, _1_cout, _2_cout, _3_cout, _4_cout, _5_cout, _6_cout, _7_cout, _8_cout, _9_cout, _10_cout,
       _11_cout, _12_cout, _13_cout, _14_cout;

  _1_bit_ALU _0 (.Cin(Cin), .A(A[0]), .B(B[0]), .RESULT(RESULT[0]), .Cout(_0_cout), .SELECT(SELECT));
  _1_bit_ALU _1 (.Cin(_0_cout), .A(A[1]), .B(B[1]), .RESULT(RESULT[1]), .Cout(_1_cout), .SELECT(SELECT));
  _1_bit_ALU _2 (.Cin(_1_cout), .A(A[2]), .B(B[2]), .RESULT(RESULT[2]), .Cout(_2_cout), .SELECT(SELECT));
  _1_bit_ALU _3 (.Cin(_2_cout), .A(A[3]), .B(B[3]), .RESULT(RESULT[3]), .Cout(_3_cout), .SELECT(SELECT));
  _1_bit_ALU _4 (.Cin(_3_cout), .A(A[4]), .B(B[4]), .RESULT(RESULT[4]), .Cout(_4_cout), .SELECT(SELECT));
  _1_bit_ALU _5 (.Cin(_4_cout), .A(A[5]), .B(B[5]), .RESULT(RESULT[5]), .Cout(_5_cout), .SELECT(SELECT));
  _1_bit_ALU _6 (.Cin(_5_cout), .A(A[6]), .B(B[6]), .RESULT(RESULT[6]), .Cout(_6_cout), .SELECT(SELECT));
  _1_bit_ALU _7 (.Cin(_6_cout), .A(A[7]), .B(B[7]), .RESULT(RESULT[7]), .Cout(_7_cout), .SELECT(SELECT));
  _1_bit_ALU _8 (.Cin(_7_cout), .A(A[8]), .B(B[8]), .RESULT(RESULT[8]), .Cout(_8_cout), .SELECT(SELECT));
  _1_bit_ALU _9 (.Cin(_8_cout), .A(A[9]), .B(B[9]), .RESULT(RESULT[9]), .Cout(_9_cout), .SELECT(SELECT));
  _1_bit_ALU _10 (.Cin(_9_cout), .A(A[10]), .B(B[10]), .RESULT(RESULT[10]), .Cout(_10_cout), .SELECT(SELECT));
  _1_bit_ALU _11 (.Cin(_10_cout), .A(A[11]), .B(B[11]), .RESULT(RESULT[11]), .Cout(_11_cout), .SELECT(SELECT));
  _1_bit_ALU _12 (.Cin(_11_cout), .A(A[12]), .B(B[12]), .RESULT(RESULT[12]), .Cout(_12_cout), .SELECT(SELECT));
  _1_bit_ALU _13 (.Cin(_12_cout), .A(A[13]), .B(B[13]), .RESULT(RESULT[13]), .Cout(_13_cout), .SELECT(SELECT));
  _1_bit_ALU _14 (.Cin(_13_cout), .A(A[14]), .B(B[14]), .RESULT(RESULT[14]), .Cout(_14_cout), .SELECT(SELECT));
  _1_bit_ALU _15 (.Cin(_14_cout), .A(A[15]), .B(B[15]), .RESULT(RESULT[15]), .Cout(Cout), .SELECT(SELECT));
  nor nor_1 (ZERO_SIGNAL, RESULT[0], RESULT[1], RESULT[2], RESULT[3], RESULT[4], RESULT[5], RESULT[6], RESULT[7], RESULT[8], RESULT[9], RESULT[10], RESULT[11], RESULT[12], RESULT[13], RESULT[14], RESULT[15]);

  // Notes on the sheet:
  //   Sudipto Roy
  //   ID: 2222756042
endmodule
